# Fritzing sketch WordClock_WS2812B (saved by Fritzing 0.9.3b)

parts:
  WeMos_D1_Mini1 = WeMos D1 Mini
  NEOPIXEL1 = Neopixel Strip -- Black (60/m)
  C1 = Electrolytic Capacitor [capacitance=0.1mF voltage=16V package="100 mil [THT, electrolytic]"]
  R1 = Resistor [tolerance=±5% resistance=10k package=THT]
  R2 = Photocell (LDR) [package=THT]
  NEOPIXEL2 = Neopixel Strip -- Black (60/m)
  NEOPIXEL3 = Neopixel Strip -- Black (60/m)
  NEOPIXEL4 = Neopixel Strip -- Black (60/m)
  NEOPIXEL5 = Neopixel Strip -- Black (60/m)
  NEOPIXEL6 = Neopixel Strip -- Black (60/m)
  NEOPIXEL7 = Neopixel Strip -- Black (60/m)
  NEOPIXEL8 = Neopixel Strip -- Black (60/m)

nets:
  N1: WeMos_D1_Mini1.3V3, R2.pin_1
  +5V: WeMos_D1_Mini1.5V, NEOPIXEL1.+5V, C1.+, NEOPIXEL2.+5V, NEOPIXEL3.+5V, NEOPIXEL4.+5V, NEOPIXEL5.+5V, NEOPIXEL6.+5V, NEOPIXEL7.+5V, NEOPIXEL8.+5V
  N2: WeMos_D1_Mini1.A0, R1.Pin_1, R2.pin_0
  N3: WeMos_D1_Mini1.D5, NEOPIXEL1.DI
  GND: WeMos_D1_Mini1.G, NEOPIXEL1.GND, C1.-, R1.Pin_0, NEOPIXEL2.GND, NEOPIXEL3.GND, NEOPIXEL4.GND, NEOPIXEL5.GND, NEOPIXEL6.GND, NEOPIXEL7.GND, NEOPIXEL8.GND
  N4: NEOPIXEL1.DO, NEOPIXEL2.DI
  N5: NEOPIXEL2.DO, NEOPIXEL4.DI
  N6: NEOPIXEL3.DI, NEOPIXEL4.DO
  N7: NEOPIXEL3.DO, NEOPIXEL6.DI
  N8: NEOPIXEL5.DI, NEOPIXEL7.DO
  N9: NEOPIXEL6.DO, NEOPIXEL8.DI
  N10: NEOPIXEL7.DI, NEOPIXEL8.DO

custom parts:
  WeMos D1 Mini: The D1 mini is a mini wifi board based on ESP-8266EX.
  Neopixel Strip -- Black (60/m): Neopixel Strip, Black, 60 pixels per meter.
